// Logisim project CircuitoLogism.circ as structural Verilog: 1 circuit, main circuit main
module main (
  input  a,
  input  b,
  input  c,
  output s
);

  wire not_1_out, or_1_out, or_2_out;

  or or_1 (or_1_out, a, b);
  not not_1 (not_1_out, b);
  or or_2 (or_2_out, not_1_out, c);
  and and_1 (s, or_1_out, or_2_out);
endmodule
